// Logisim project led light.circ as structural Verilog
module main (
  input  j,
  input  k,
  input  l,
  input  in_4
);

  wire A_out, B_out, C_out, D_out, E_out, F_out, G_out, i_prime_j_out, i_prime_j_prime_k_out,
       i_prime_j_prime_k_prime_l_prime_out, i_prime_j_prime_k_prime_out, i_prime_j_prime_kl_out,
       i_prime_j_prime_out, i_prime_jk_prime_l_out, i_prime_jkl_out, i_prime_k_prime_jl_2_out,
       i_prime_k_prime_jl_3_out, i_prime_k_prime_jl_out, i_prime_k_prime_l_prime_j_out,
       i_prime_l_prime_j_out, i_prime_l_prime_jk_out, j_prime_k_out, j_prime_k_prime_l_prime_2_out,
       j_prime_k_prime_l_prime_out, k_prime_l_prime_out, kl_prime_2_out, kl_prime_out, not_1_out, not_2_out,
       not_3_out, not_4_out, not_5_out, not_6_out, not_7_out, not_8_out, not_9_out;

  not not_1 (not_1_out, j);
  not not_2 (not_2_out, k);
  not not_3 (not_3_out, l);
  not not_4 (not_4_out, in_4);
  and i_prime_j_prime_k (i_prime_j_prime_k_out, not_1_out, not_2_out, l);
  and kl_prime (kl_prime_out, l, not_4_out);
  and i_prime_l_prime_j (i_prime_l_prime_j_out, not_1_out, not_4_out, k);
  and j_prime_k_prime_l_prime (j_prime_k_prime_l_prime_out, not_2_out, not_3_out, not_4_out);
  and k_prime_l_prime (k_prime_l_prime_out, not_7_out, not_8_out);
  and i_prime_j_prime (i_prime_j_prime_out, not_1_out, not_2_out);
  and i_prime_k_prime_jl (i_prime_k_prime_jl_out, not_1_out, not_3_out, k, in_4);
  or E (E_out, kl_prime_out, j_prime_k_prime_l_prime_out);
  not not_5 (not_5_out, j);
  not not_6 (not_6_out, k);
  not not_7 (not_7_out, l);
  not not_8 (not_8_out, in_4);
  and i_prime_l_prime_jk (i_prime_l_prime_jk_out, not_5_out, not_8_out, k, l);
  and i_prime_jkl (i_prime_jkl_out, not_1_out, k, l, in_4);
  or D (D_out, j, i_prime_j_prime_k_out, i_prime_l_prime_j_out, i_prime_k_prime_jl_out);
  and i_prime_j (i_prime_j_out, not_5_out, k);
  and i_prime_j_prime_k_prime (i_prime_j_prime_k_prime_out, not_5_out, not_6_out, not_7_out);
  and i_prime_j_prime_k_prime_l_prime (i_prime_j_prime_k_prime_l_prime_out, not_5_out, not_6_out, not_7_out, not_8_out);
  and i_prime_jk_prime_l (i_prime_jk_prime_l_out, k, not_5_out, not_7_out, in_4);
  and i_prime_k_prime_jl_2 (i_prime_k_prime_jl_2_out, not_5_out, not_7_out, k, in_4);
  and i_prime_k_prime_l_prime_j (i_prime_k_prime_l_prime_j_out, not_5_out, not_3_out, not_4_out, k);
  and i_prime_j_prime_kl (i_prime_j_prime_kl_out, not_5_out, not_6_out, l, in_4);
  or A (A_out, l, j, i_prime_j_prime_k_prime_l_prime_out, i_prime_jk_prime_l_out);
  or B (B_out, j, k_prime_l_prime_out, i_prime_l_prime_jk_out, i_prime_k_prime_jl_2_out);
  or C (C_out, j, i_prime_j_prime_out, i_prime_jkl_out, i_prime_k_prime_l_prime_j_out);
  _7_Segment_Display u_7_segment_display_1 (
    .g(D_out), .f(B_out), .a(A_out), .b(C_out), .e(E_out), .d(G_out), .c(F_out));  // open: dp
  or F (F_out, j, i_prime_j_out, i_prime_j_prime_k_prime_out, i_prime_j_prime_kl_out);
  not not_9 (not_9_out, l);
  and j_prime_k (j_prime_k_out, not_6_out, l);
  and j_prime_k_prime_l_prime_2 (j_prime_k_prime_l_prime_2_out, not_6_out, not_7_out, not_8_out);
  and kl_prime_2 (kl_prime_2_out, l, not_8_out);
  and i_prime_k_prime_jl_3 (i_prime_k_prime_jl_3_out, not_5_out, not_9_out, k, in_4);
  or G (G_out, j_prime_k_out, j_prime_k_prime_l_prime_2_out, kl_prime_2_out, i_prime_k_prime_jl_3_out);

  // Notes on the sheet:
  //   i
endmodule
